# Fritzing sketch oc_Atmega328 (saved by Fritzing 0.9.3b)
breadboards: 1

parts:
  Arduino1 = Arduino Mini (Rev5)
  S1 = Pushbutton [package="[THT]"]
  S2 = Pushbutton [package="[THT]"]
  S3 = Pushbutton [package="[THT]"]
  R1 = Resistor [tolerance=±5% resistance=220 package=THT]
  R2 = Resistor [tolerance=±5% resistance=220 package=THT]
  R3 = Resistor [tolerance=±5% resistance=220 package=THT]
  J1 = Piezo Speaker

nets:
  N1: Arduino1.D3_PWM, J1.pin2
  N2: Arduino1.D7, S3.Pin_3, S3.Pin_4
  N3: Arduino1.D8, S2.Pin_3, S2.Pin_4
  N4: Arduino1.D9_PWM, S1.Pin_3, S1.Pin_4
  N5: S1.Pin_1, S1.Pin_2, R1.Pin_0
  N6: S2.Pin_1, S2.Pin_2, R2.Pin_0
  N7: S3.Pin_1, S3.Pin_2, R3.Pin_0
  N8: R1.Pin_1, R2.Pin_1, R3.Pin_1, J1.pin1
